// Logisim project STEP SELEC.circ as structural Verilog: 1 circuit, main circuit main
module main (
  input  [7:0] in_1,
  input  [7:0] in_2,
  input  [7:0] in_3,
  output [7:0] out_4
);

  wire and_1_out, and_2_out, and_3_out, and_4_out, and_5_out, and_6_out, and_7_out;
  wire [7:0] and_9_out, and_10_out, not_1_out;
  wire [7:7] and_8_out;

  and and_1 (and_1_out, in_1[7], 1'b1);
  and and_2 (and_2_out, in_1[6], and_1_out);
  and and_3 (and_3_out, in_1[5], and_2_out);
  and and_4 (and_4_out, in_1[4], and_3_out);
  and and_5 (and_5_out, in_1[3], and_4_out);
  and and_6 (and_6_out, in_1[1], and_7_out);
  and and_7 (and_7_out, in_1[2], and_5_out);
  and and_8 (and_8_out[7], in_1[0], and_6_out);
  assign not_1_out = ~{8{and_8_out[7]}};  // NOT_Gate not_1, 8 bits wide
  assign and_9_out = in_2 & not_1_out;  // AND_Gate and_9, 8 bits wide
  assign and_10_out = {8{and_8_out[7]}} & in_3;  // AND_Gate and_10, 8 bits wide
  assign out_4 = and_9_out | and_10_out;  // OR_Gate or_1, 8 bits wide
endmodule
