// Logisim project rcd.circ as structural Verilog: 1 circuit, main circuit main
module main (
  input  [7:0] in_1,
  input  [7:0] in_2,
  input  [7:0] in_3,
  output [7:0] out_4,
  output [7:0] out_5,
  output [7:0] out_6,
  output [7:0] out_7,
  output [7:0] out_8,
  output [7:0] Input_stream
);

  wire and_1_out, button_1_out, button_2_out, clock_1_out, not_1_out, not_2_out, not_3_out, or_1_out;
  wire [3:0] main_1_p1, main_1_p2, main_1_p4, main_2_p1, main_2_p2, main_2_p4, main_3_p1, main_3_p2,
       main_3_p4;
  wire [7:0] counter_1_q, main_1_p3, main_2_p3, main_3_p3, main_6_out_4, main_7_to_a, main_7_to_b,
       main_7_to_c, main_8_out_3, main_9_out_3, main_10_out_3, main_11_out_3, main_12_out_3, main_13_out_3,
       main_14_out_3, main_15_out_3, main_18_out_8, main_18_out_9, main_18_out_10, main_19_out_8,
       main_19_out_9, main_19_out_10, main_20_out_8, main_20_out_9, main_20_out_10, main_21_out_8,
       main_21_out_9, main_21_out_10, main_22_out_8, main_22_out_9, main_22_out_10, main_23_out_8,
       main_23_out_9, main_23_out_10, main_24_out_8, main_24_out_9, main_24_out_10, main_25_out_8,
       main_25_out_9, main_25_out_10, main_26_out_8, main_26_out_9, main_26_out_10;
  wire [8:0] rom_1_data_2;
  wire [14:0] main_4_out_2;
  wire [17:0] rom_1_data;
  wire [23:0] and_2_out, and_3_out, controlled_buffer_1_out, controlled_buffer_2_out;
  wire [23:23] and_4_out, main_4_out_2_2;
  wire [31:27] rom_1_data_3;

  Hex_Digit_Display hex_digit_display_1 (.value(main_1_p1));  // open: dp
  Button button_1 (.out(button_1_out));
  Button button_2 (.out(button_2_out));
  Clock clock_1 (.out(clock_1_out));
  Hex_Digit_Display hex_digit_display_2 (.value(main_1_p2));  // open: dp
  Hex_Digit_Display hex_digit_display_3 (.value(main_1_p4));  // open: dp
  // BIN2DEC_main main_1: pin names not known; wires that end beside it: main_1_p1, main_1_p2, main_1_p3, main_1_p4
  not not_1 (not_1_out, main_4_out_2[9]);
  and and_1 (and_1_out, clock_1_out, not_2_out);
  or or_1 (or_1_out, button_2_out, and_1_out);
  Hex_Digit_Display hex_digit_display_4 (.value(main_2_p1));  // open: dp
  Counter counter_1 (
    .load(main_4_out_2[9]), .D(main_6_out_4), .count(not_1_out), .Q(counter_1_q), .clk(or_1_out),
    .clr(button_1_out));  // open: carry
  not not_2 (not_2_out, rom_1_data_3[31]);
  Hex_Digit_Display hex_digit_display_5 (.value(main_2_p2));  // open: dp
  Hex_Digit_Display hex_digit_display_6 (.value(main_2_p4));  // open: dp
  // BIN2DEC_main main_2: pin names not known; wires that end beside it: main_2_p1, main_2_p2, main_2_p3, main_2_p4
  Hex_Digit_Display hex_digit_display_7 (.value(main_3_p1));  // open: dp
  Hex_Digit_Display hex_digit_display_8 (.value(main_3_p2));  // open: dp
  // BIN2DEC_main main_3: pin names not known; wires that end beside it: main_3_p1, main_3_p2, main_3_p3, main_3_p4
  assign {main_1_p3, main_2_p3, main_3_p3} = and_2_out | and_3_out;  // OR_Gate or_2, 24 bits wide
  ROM #(.dataWidth(32)) rom_1 (.addr(counter_1_q), .data({rom_1_data_3, rom_1_data_2, rom_1_data}));  // open: sel
  Hex_Digit_Display hex_digit_display_9 (.value(main_3_p4));  // open: dp
  assign controlled_buffer_1_out = main_4_out_2_2[23] ? {out_4, out_6, out_8} : 24'bz;  // Controlled_Buffer controlled_buffer_1
  assign and_2_out = {24{and_4_out[23]}} & controlled_buffer_2_out;  // AND_Gate and_2, 24 bits wide
  assign and_3_out = controlled_buffer_1_out & {24{main_4_out_2_2[23]}};  // AND_Gate and_3, 24 bits wide
  INSTRCTR_main main_4 (
    .in_1(rom_1_data_3[30:27]), .out_2({main_4_out_2[14:12], main_4_out_2_2[23], main_4_out_2[10:0]}));
  RAM_main main_5 (
    .out_5(out_4), .in_1({rom_1_data_2[8:7], 1'b0, rom_1_data_2[6:0]}), .in_2(or_1_out), .in_3(out_5),
    .in_4(button_1_out));
  assign controlled_buffer_2_out = rom_1_data_3[31] ? {in_3, in_2, in_1} : 24'bz;  // Controlled_Buffer controlled_buffer_2
  STEP_SELEC_main main_6 (.in_2(out_4), .in_3(out_6), .out_4(main_6_out_4), .in_1(out_8));
  VAL_TRNSFR_main main_7 (
    .Inp_A(out_4), .Inp_C(out_8), .Inp_B(out_6), .To_B(main_7_to_b), .To_A(main_7_to_a), .To_C(main_7_to_c));
  SFTRGT_main main_8 (.in_1(out_4), .in_2(out_6), .out_3(main_8_out_3));
  SFTLFT_main main_9 (.in_1(out_4), .in_2(out_6), .out_3(main_9_out_3));
  XNOR_main main_10 (.in_1(out_4), .in_2(out_6), .out_3(main_10_out_3));
  XOR_main main_11 (.in_1(out_4), .in_2(out_6), .out_3(main_11_out_3));
  NOR_main main_12 (.in_1(out_4), .in_2(out_6), .out_3(main_12_out_3));
  NAND_main main_13 (.in_1(out_4), .in_2(out_6), .out_3(main_13_out_3));
  OR_main main_14 (.in_1(out_4), .in_2(out_6), .out_3(main_14_out_3));
  AND_main main_15 (.in_1(out_4), .in_2(out_6), .out_3(main_15_out_3));
  and and_4 (and_4_out[23], rom_1_data_3[31], not_3_out);
  not not_3 (not_3_out, main_4_out_2_2[23]);
  RAM_main main_16 (
    .out_5(out_6), .in_1({rom_1_data[17:16], 1'b0, rom_1_data[15:9]}), .in_2(or_1_out), .in_3(out_7),
    .in_4(button_1_out));
  RAM_main main_17 (
    .out_5(out_8), .in_1({rom_1_data[8:7], 1'b0, rom_1_data[6:0]}), .in_2(or_1_out), .in_3(Input_stream),
    .in_4(button_1_out));
  INP_SEL_main main_18 (
    .in_1({8{1'b0}}), .in_2({8{1'b0}}), .in_3({8{1'b0}}), .in_4(main_4_out_2[10]), .out_8(main_18_out_8),
    .out_9(main_18_out_9), .out_10(main_18_out_10), .in_5(in_1), .in_6(in_2), .in_7(in_3));
  INP_SEL_main main_19 (
    .in_1(main_18_out_8), .in_2(main_18_out_9), .in_3(main_18_out_10), .in_4(main_4_out_2[8]),
    .out_8(main_19_out_8), .out_9(main_19_out_9), .out_10(main_19_out_10), .in_5(main_7_to_a),
    .in_6(main_7_to_b), .in_7(main_7_to_c));
  INP_SEL_main main_20 (
    .in_1(main_19_out_8), .in_2(main_19_out_9), .in_3(main_19_out_10), .in_4(main_4_out_2[7]),
    .out_8(main_20_out_8), .out_9(main_20_out_9), .out_10(main_20_out_10), .in_5({8{1'b0}}),
    .in_6({8{1'b0}}), .in_7(main_8_out_3));
  INP_SEL_main main_21 (
    .in_1(main_20_out_8), .in_2(main_20_out_9), .in_3(main_20_out_10), .in_4(main_4_out_2[6]),
    .out_8(main_21_out_8), .out_9(main_21_out_9), .out_10(main_21_out_10), .in_5({8{1'b0}}),
    .in_6({8{1'b0}}), .in_7(main_9_out_3));
  INP_SEL_main main_22 (
    .in_1(main_21_out_8), .in_2(main_21_out_9), .in_3(main_21_out_10), .in_4(main_4_out_2[5]),
    .out_8(main_22_out_8), .out_9(main_22_out_9), .out_10(main_22_out_10), .in_5({8{1'b0}}),
    .in_6({8{1'b0}}), .in_7(main_10_out_3));
  INP_SEL_main main_23 (
    .in_1(main_22_out_8), .in_2(main_22_out_9), .in_3(main_22_out_10), .in_4(main_4_out_2[4]),
    .out_8(main_23_out_8), .out_9(main_23_out_9), .out_10(main_23_out_10), .in_5({8{1'b0}}),
    .in_6({8{1'b0}}), .in_7(main_11_out_3));
  INP_SEL_main main_24 (
    .in_1(main_23_out_8), .in_2(main_23_out_9), .in_3(main_23_out_10), .in_4(main_4_out_2[3]),
    .out_8(main_24_out_8), .out_9(main_24_out_9), .out_10(main_24_out_10), .in_5({8{1'b0}}),
    .in_6({8{1'b0}}), .in_7(main_12_out_3));
  INP_SEL_main main_25 (
    .in_1(main_24_out_8), .in_2(main_24_out_9), .in_3(main_24_out_10), .in_4(main_4_out_2[2]),
    .out_8(main_25_out_8), .out_9(main_25_out_9), .out_10(main_25_out_10), .in_5({8{1'b0}}),
    .in_6({8{1'b0}}), .in_7(main_13_out_3));
  INP_SEL_main main_26 (
    .in_1(main_25_out_8), .in_2(main_25_out_9), .in_3(main_25_out_10), .in_4(main_4_out_2[1]),
    .out_8(main_26_out_8), .out_9(main_26_out_9), .out_10(main_26_out_10), .in_5({8{1'b0}}),
    .in_6({8{1'b0}}), .in_7(main_14_out_3));
  INP_SEL_main main_27 (
    .in_1(main_26_out_8), .in_2(main_26_out_9), .in_3(main_26_out_10), .in_4(main_4_out_2[0]), .out_8(out_5),
    .out_9(out_7), .out_10(Input_stream), .in_5({8{1'b0}}), .in_6({8{1'b0}}), .in_7(main_15_out_3));

  // Notes on the sheet:
  //   Reset
  //   Go
  //   A
  //   B
  //   C
  //   Output stream
  //   contents of rom_1 (hex, n*v repeats v):
  //   80000000 5c060c00 4f020400 a050501 4c080081 32090501 56270e81 120f0301 4c0c0081 20c0000 56480000
  //   3a0c0101 4c0c0081 40010501 48020481 36010501 560f2281 57100000 4c150c00 4f020600 a0d0701 a150702
  //   4c1c0081 4c100082 321d0701 32110702 566f3881 56777e82 568b3a82 40010703 48020683 36010703 56874483
  //   56530180 4a0c0106 0 4c200086 4a160800 26010904 48020884 4c240181 2a250904 a250905 4c240084 48020885
  //   38010905 48020885 36010904 56a76284 4a260800 2a210904 a210905 4c200084 48020885 38010905 48020885
  //   36010904 56cb7484 2200000 4a200107 4c0c0087 122b0308 4c280088 0 3a280108 4c280088 2280000 562c0000
  //   42280108 4c280088 4a200108 48020a88 e2290a00
  //   CAUTION: 7 BIT MAX ONLY
endmodule
